# Fritzing sketch bean-unashield (saved by Fritzing 0.9.3b)

parts:
  Part1 = UnaBiz UnaShield
  Part2 = LightBlue Bean+

nets:
  GND: Part1.GND, Part2.GND, Part2.Grove_A2/A3
  N1: Part1.D4, Part2.D4
  N2: Part1.D5_PWM, Part2.D5
  3V3: Part1.3V3, Part2.3.3V
  5V: Part1.5V, Part2.5V

notes:
  Select 5V

custom parts:
  UnaBiz UnaShield: UnaShield is an Arduino Shield with a SIGFOX transceiver module that is compatible with Arduino Uno and other Arduino-based boards. It uses the Radiocrafts module certified for RCZ4 (Singapore, Taiwan, Australia, New Zealand, South America). The UnaBiz team has built an Arduino library for the UnaShield, the source code may be found here: https://github.com/UnaBiz/unabiz-arduino Here's a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
  LightBlue Bean+: http://store.punchthrough.com/collections/all/products/lightblue-bean-plus
